# Fritzing sketch Gleisbesetzmeldung (saved by Fritzing 0.9.3b)
breadboards: 1

parts:
  IC1 = IC, DIP package, 6 pins [chip_label=IC part_number=CNY-17-2]
  Q1 = NPN-Transistor [part_number=2N2222 package="TO92 [THT]"]
  R2 = Resistor [tolerance=±5% resistance=1k package=THT]
  JP3 = Header 2 [package=molex-1x2_lock]
  R1 = Resistor [tolerance=±5% resistance=1k package=THT]
  JP4 = Header 2 [package=molex-1x2_lock]

nets (from the schematic view):
  N1: IC1.pin1, R1.Pin_1
  N2: IC1.pin2, JP3.2
  GND: IC1.pin4, Q1.E
  N3: IC1.pin5, Q1.B, R2.Pin_0
  5V: Q1.C, R2.Pin_1, JP4.1
